// Logisim project PRESENT.circ as structural Verilog: 1 circuit, main circuit main
module main (
  input  [15:0] in_1,
  input  [31:0] in_2,
  input  [31:0] in_3,
  input  [31:0] in_4,
  input  [31:0] in_5,
  input  in_6,
  input  in_7,
  input  in_8,
  input  in_9,
  output [31:0] out_10,
  output [31:0] out_11,
  output [31:0] out_12
);

  wire clock_1_out, not_1_out;
  wire [2:0] counter_1_q;
  wire [15:0] main_4_out_6, multiplexer_3_out;
  wire [31:0] buffer_1_out, counter_2_q, main_1_p2, main_1_p4, main_2_out_4, main_2_out_5, main_3_out_4,
       main_3_out_5, main_4_out_5, main_4_out_7, multiplexer_1_out, multiplexer_2_out, multiplexer_4_out,
       multiplexer_5_out, xor_1_out, xor_3_out;

  assign xor_1_out = in_2 ^ main_2_out_4;  // XOR_Gate xor_1, 32 bits wide
  Multiplexer #(.width(32)) multiplexer_1 (.in0(xor_1_out), .in1(out_10), .out(multiplexer_1_out));  // open: sel, en
  assign out_10 = main_1_p2 ^ main_3_out_4;  // XOR_Gate xor_2, 32 bits wide
  assign xor_3_out = in_3 ^ main_2_out_5;  // XOR_Gate xor_3, 32 bits wide
  Multiplexer #(.width(32)) multiplexer_2 (.in0(xor_3_out), .in1(out_11), .out(multiplexer_2_out));  // open: sel, en
  // SPNet_main main_1: pin names not known; wires that end beside it: multiplexer_1_out, main_1_p2, multiplexer_2_out, main_1_p4
  Counter #(.width(3), .max('h7)) counter_1 (
    .count(in_6), .Q(counter_1_q), .clk(clock_1_out));  // open: load, D, carry, clr
  Counter #(.width(32), .max('hffffffff)) counter_2 (
    .load(in_6), .count(in_7), .Q(counter_2_q), .clk(clock_1_out));  // open: D, carry, clr
  assign out_11 = main_1_p4 ^ main_3_out_5;  // XOR_Gate xor_4, 32 bits wide
  SelectKey_main main_2 (.in_3(in_1), .in_1(in_4), .in_2(in_5), .out_4(main_2_out_4), .out_5(main_2_out_5));
  SelectKey_main main_3 (
    .in_3(main_4_out_6), .in_1(main_4_out_5), .in_2(main_4_out_7), .out_4(main_3_out_4), .out_5(main_3_out_5));
  assign buffer_1_out = counter_2_q;  // Buffer buffer_1, 32 bits wide
  Clock clock_1 (.out(clock_1_out));
  Multiplexer #(.width(16)) multiplexer_3 (.in0(in_1), .in1(main_4_out_6), .out(multiplexer_3_out));  // open: sel, en
  RAM #(.addrWidth(3), .dataWidth(32), .bus("separate")) ram_1 (
    .addr(counter_1_q), .din(buffer_1_out), .data(out_12), .str(clock_1_out), .sel(in_8), .clk(clock_1_out),
    .ld(not_1_out), .clr(in_9));
  not not_1 (not_1_out, clock_1_out);
  Multiplexer #(.width(32)) multiplexer_4 (.in0(in_4), .in1(main_4_out_5), .out(multiplexer_4_out));  // open: sel, en
  KeyT_main main_4 (
    .in_1(multiplexer_3_out), .in_2(multiplexer_4_out), .in_3(multiplexer_5_out), .out_6(main_4_out_6),
    .out_5(main_4_out_5), .out_7(main_4_out_7));  // open: counter
  Multiplexer #(.width(32)) multiplexer_5 (.in0(in_5), .in1(main_4_out_7), .out(multiplexer_5_out));  // open: sel, en

  // Notes on the sheet:
  //   out_12: pull=down
  //   add Round Key
  //   select Key
  //   select Key
  //   ticks enable
  //   when str and sel is 1 then value at west edge is transferred to the RAM
  //   when ld and sel is 1 then value from selected address goes into east side D
endmodule
